// Logisim project UDEA_DISPLAY.circ as structural Verilog
module UDEA (
  input  G,
  input  F,
  input  A,
  input  B,
  input  [3:0] in_5,
  input  [3:0] in_6,
  input  [3:0] in_7,
  input  E,
  input  D,
  input  C
);

  _7_Segment_Display u_7_segment_display_1 (.g(G), .f(F), .a(A), .b(B), .e(E), .d(D), .c(C));  // open: dp
  Hex_Digit_Display hex_digit_display_1 (.value(in_5));  // open: dp
  Hex_Digit_Display hex_digit_display_2 (.value(in_6));  // open: dp
  Hex_Digit_Display hex_digit_display_3 (.value(in_7));  // open: dp
endmodule
