// Logisim project METRO.circ as structural Verilog
module MUX4X1 (
  input  C0,
  input  C1,
  input  E0,
  input  E1,
  input  E2,
  input  E3,
  output S
);

  wire and_1_out, and_2_out, and_3_out, and_5_out, not_1_out, not_2_out;

  not not_1 (not_1_out, C0);
  not not_2 (not_2_out, C1);
  and and_1 (and_1_out, not_1_out, not_2_out, E0);
  and and_2 (and_2_out, C0, not_2_out, E1);
  and and_3 (and_3_out, not_1_out, C1, E2);
  // AND_Gate and_4 is placed but not wired
  and and_5 (and_5_out, C0, C1, E3);
  // AND_Gate and_6 is placed but not wired
  or or_1 (S, and_1_out, and_2_out, and_3_out, and_5_out);
endmodule

module MUX2X1 (
  input  E0,
  input  C0,
  input  E1,
  output out_4
);

  wire nand_1_out, nand_2_out, nand_3_out;

  nand nand_1 (nand_1_out, C0, C0);
  nand nand_2 (nand_2_out, E0, C0);
  nand nand_3 (nand_3_out, nand_1_out, E1);
  nand nand_4 (out_4, nand_2_out, nand_3_out);
endmodule

module MUX8X1 (
  input  E0,
  input  E1,
  input  E2,
  input  E3,
  input  E4,
  input  E5,
  input  E6,
  input  E7,
  input  C0,
  input  C1,
  input  C2,
  output S
);

  wire mux4x1_1_s, mux4x1_2_s;

  MUX4X1 mux4x1_1 (.C0(C0), .C1(C1), .E0(E0), .E1(E1), .E2(E2), .E3(E3), .S(mux4x1_1_s));
  MUX4X1 mux4x1_2 (.C0(C0), .C1(C1), .E0(E4), .E1(E5), .E2(E6), .E3(E7), .S(mux4x1_2_s));
  MUX2X1 mux2x1_1 (.E0(mux4x1_2_s), .C0(C2), .E1(mux4x1_1_s), .out_4(S));
endmodule

module DECO7SEG (
  input  in_1,
  input  in_2,
  input  in_3,
  input  A,
  output out_5,
  output b,
  output c,
  output d,
  output e,
  output f,
  output g
);

  wire nand_1_out, nand_2_out, nand_3_out, nand_4_out, nand_5_out, nand_6_out, nand_7_out, nand_8_out,
       nand_9_out, nand_10_out, nand_11_out, nand_12_out, nand_13_out, nand_14_out, nand_15_out, nand_16_out,
       nand_17_out, nand_18_out, nand_19_out, nand_20_out, nand_21_out, nand_22_out, nand_23_out,
       nand_24_out, nand_25_out, nand_26_out, nand_27_out, nand_28_out, nand_29_out, nand_30_out,
       nand_31_out, nand_32_out, nand_33_out, nand_34_out, nand_35_out, nand_36_out, nand_37_out,
       nand_38_out, nand_39_out, nand_40_out, nand_41_out, nand_42_out, nand_43_out, nand_44_out,
       nand_45_out, nand_46_out, nand_47_out, nand_48_out, nand_49_out, nand_50_out, nand_51_out,
       nand_52_out, nand_53_out, nand_54_out, nand_55_out, nand_56_out, nand_57_out, nand_58_out,
       nand_59_out, nand_60_out, nand_61_out, nand_62_out, nand_63_out, nand_64_out, nand_65_out,
       nand_66_out, nand_67_out, nand_68_out, nand_69_out, nand_70_out, nand_71_out, nand_72_out,
       nand_73_out, nand_74_out, nand_75_out, nand_76_out, nand_77_out, nand_78_out, nand_79_out,
       nand_80_out, nand_81_out, nand_82_out, nand_83_out, nand_84_out, nand_85_out, nand_86_out,
       nand_87_out, nand_88_out, nand_89_out, nand_90_out, nand_91_out, nand_92_out, nand_93_out,
       nand_94_out, nand_95_out, nand_96_out, nand_97_out, nand_98_out, nand_99_out, nand_100_out,
       nand_101_out, nand_102_out, nand_103_out, nand_104_out, nand_106_out, nand_107_out, nand_108_out,
       nand_109_out, nand_110_out, nand_111_out, nand_112_out, nand_113_out, nand_114_out, nand_115_out,
       nand_116_out, nand_117_out, nand_118_out, nand_119_out, nand_120_out, nand_121_out, nand_122_out,
       nand_123_out, nand_124_out, nand_125_out, nand_126_out, nand_127_out, nand_128_out, nand_129_out,
       nand_130_out, nand_131_out, nand_132_out, nand_133_out, nand_134_out, nand_136_out, nand_137_out,
       nand_138_out, nand_139_out, nand_141_out, nand_142_out, nand_143_out, nand_144_out, nand_145_out,
       nand_146_out, nand_147_out, nand_148_out;

  nand nand_1 (nand_1_out, in_2, in_2);
  nand nand_2 (nand_2_out, in_1, in_1);
  nand nand_3 (nand_3_out, in_3, in_3);
  nand nand_4 (nand_4_out, in_1, in_1);
  nand nand_5 (nand_5_out, in_3, in_3);
  nand nand_6 (nand_6_out, in_1, in_1);
  nand nand_7 (nand_7_out, in_1, in_1);
  nand nand_8 (nand_8_out, in_2, in_2);
  nand nand_9 (nand_9_out, in_2, in_2);
  nand nand_10 (nand_10_out, in_2, in_2);
  nand nand_11 (nand_11_out, A, A);
  nand nand_12 (nand_12_out, A, A);
  nand nand_13 (nand_13_out, in_1, in_1);
  nand nand_14 (nand_14_out, in_2, in_2);
  nand nand_15 (nand_15_out, A, A);
  nand nand_16 (nand_16_out, in_1, in_1);
  nand nand_17 (nand_17_out, in_1, nand_1_out);
  nand nand_18 (nand_18_out, nand_2_out, nand_3_out);
  nand nand_19 (nand_19_out, nand_4_out, nand_5_out);
  nand nand_20 (nand_20_out, nand_6_out, A);
  nand nand_21 (nand_21_out, nand_7_out, nand_8_out);
  nand nand_22 (nand_22_out, nand_9_out, in_3);
  nand nand_23 (nand_23_out, nand_10_out, nand_11_out);
  nand nand_24 (nand_24_out, in_3, nand_12_out);
  nand nand_25 (nand_25_out, in_1, in_3);
  nand nand_26 (nand_26_out, in_1, in_2);
  nand nand_27 (nand_27_out, nand_13_out, in_2);
  nand nand_28 (nand_28_out, nand_14_out, in_3);
  nand nand_29 (nand_29_out, in_3, nand_15_out);
  nand nand_30 (nand_30_out, nand_16_out, in_2);
  nand nand_31 (nand_31_out, in_2, in_2);
  nand nand_32 (nand_32_out, A, A);
  nand nand_33 (nand_33_out, in_1, in_1);
  nand nand_34 (nand_34_out, in_1, in_1);
  nand nand_35 (nand_35_out, nand_17_out, nand_17_out);
  nand nand_36 (nand_36_out, in_3, in_3);
  nand nand_37 (nand_37_out, in_1, in_1);
  nand nand_38 (nand_38_out, in_2, in_2);
  nand nand_39 (nand_39_out, nand_18_out, nand_18_out);
  nand nand_40 (nand_40_out, A, A);
  nand nand_41 (nand_41_out, in_1, in_1);
  nand nand_42 (nand_42_out, in_3, in_3);
  nand nand_43 (nand_43_out, nand_19_out, nand_20_out);
  nand nand_44 (nand_44_out, in_3, in_3);
  nand nand_45 (nand_45_out, in_1, in_1);
  nand nand_46 (nand_46_out, in_2, in_2);
  nand nand_47 (nand_47_out, nand_21_out, nand_21_out);
  nand nand_48 (nand_48_out, A, A);
  nand nand_49 (nand_49_out, nand_22_out, nand_22_out);
  nand nand_50 (nand_50_out, in_3, in_3);
  nand nand_51 (nand_51_out, in_3, in_3);
  nand nand_52 (nand_52_out, nand_23_out, nand_24_out);
  nand nand_53 (nand_53_out, nand_25_out, nand_26_out);
  nand nand_54 (nand_54_out, in_3, in_3);
  nand nand_55 (nand_55_out, A, A);
  nand nand_56 (nand_56_out, nand_27_out, nand_27_out);
  nand nand_57 (nand_57_out, in_3, in_3);
  nand nand_58 (nand_58_out, nand_28_out, nand_29_out);
  nand nand_59 (nand_59_out, nand_30_out, nand_30_out);
  nand nand_60 (nand_60_out, in_3, in_3);
  nand nand_61 (nand_61_out, in_2, in_2);
  nand nand_62 (nand_62_out, nand_31_out, nand_32_out);
  nand nand_63 (nand_63_out, nand_33_out, in_3);
  nand nand_64 (nand_64_out, nand_34_out, in_2);
  nand nand_65 (nand_65_out, in_2, in_3);
  nand nand_66 (nand_66_out, nand_35_out, nand_36_out);
  nand nand_67 (nand_67_out, nand_37_out, nand_38_out);
  nand nand_68 (nand_68_out, nand_39_out, nand_40_out);
  nand nand_69 (nand_69_out, nand_41_out, in_3);
  nand nand_70 (nand_70_out, in_1, nand_42_out);
  nand nand_71 (nand_71_out, nand_43_out, nand_43_out);
  nand nand_72 (nand_72_out, nand_44_out, A);
  nand nand_73 (nand_73_out, nand_45_out, in_2);
  nand nand_74 (nand_74_out, in_1, nand_46_out);
  nand nand_75 (nand_75_out, nand_47_out, nand_48_out);
  nand nand_76 (nand_76_out, nand_49_out, A);
  nand nand_77 (nand_77_out, in_2, nand_50_out);
  nand nand_78 (nand_78_out, in_2, in_3);
  nand nand_79 (nand_79_out, in_1, nand_51_out);
  nand nand_80 (nand_80_out, nand_52_out, nand_52_out);
  nand nand_81 (nand_81_out, nand_53_out, nand_53_out);
  nand nand_82 (nand_82_out, nand_54_out, nand_55_out);
  nand nand_83 (nand_83_out, nand_56_out, nand_57_out);
  nand nand_84 (nand_84_out, nand_58_out, nand_58_out);
  nand nand_85 (nand_85_out, nand_59_out, nand_60_out);
  nand nand_86 (nand_86_out, in_1, nand_61_out);
  nand nand_87 (nand_87_out, in_1, A);
  nand nand_88 (nand_88_out, nand_62_out, nand_63_out);
  nand nand_89 (nand_89_out, nand_64_out, nand_64_out);
  nand nand_90 (nand_90_out, nand_65_out, nand_66_out);
  nand nand_91 (nand_91_out, A, A);
  nand nand_92 (nand_92_out, nand_67_out, nand_68_out);
  nand nand_93 (nand_93_out, in_2, in_2);
  nand nand_94 (nand_94_out, A, A);
  nand nand_95 (nand_95_out, nand_69_out, nand_69_out);
  nand nand_96 (nand_96_out, nand_70_out, nand_70_out);
  nand nand_97 (nand_97_out, nand_71_out, nand_72_out);
  nand nand_98 (nand_98_out, nand_73_out, nand_74_out);
  nand nand_99 (nand_99_out, nand_75_out, nand_76_out);
  nand nand_100 (nand_100_out, nand_77_out, nand_77_out);
  nand nand_101 (nand_101_out, nand_78_out, nand_78_out);
  nand nand_102 (nand_102_out, A, A);
  nand nand_103 (nand_103_out, nand_79_out, nand_79_out);
  nand nand_104 (nand_104_out, A, A);
  nand nand_105 (e, nand_80_out, nand_81_out);
  nand nand_106 (nand_106_out, nand_82_out, nand_83_out);
  nand nand_107 (nand_107_out, A, A);
  nand nand_108 (nand_108_out, in_2, in_2);
  nand nand_109 (nand_109_out, nand_84_out, nand_85_out);
  nand nand_110 (nand_110_out, nand_86_out, nand_87_out);
  nand nand_111 (nand_111_out, nand_88_out, nand_88_out);
  nand nand_112 (nand_112_out, nand_89_out, A);
  nand nand_113 (nand_113_out, nand_90_out, nand_90_out);
  nand nand_114 (nand_114_out, in_1, nand_91_out);
  nand nand_115 (nand_115_out, nand_92_out, nand_92_out);
  nand nand_116 (nand_116_out, nand_93_out, nand_94_out);
  nand nand_117 (nand_117_out, nand_95_out, A);
  nand nand_118 (nand_118_out, nand_96_out, A);
  nand nand_119 (nand_119_out, nand_97_out, nand_97_out);
  nand nand_120 (nand_120_out, nand_98_out, nand_98_out);
  nand nand_121 (nand_121_out, nand_99_out, nand_99_out);
  nand nand_122 (nand_122_out, nand_100_out, A);
  nand nand_123 (nand_123_out, nand_101_out, nand_102_out);
  nand nand_124 (nand_124_out, nand_103_out, nand_104_out);
  nand nand_125 (nand_125_out, nand_106_out, nand_106_out);
  nand nand_126 (nand_126_out, in_2, nand_107_out);
  nand nand_127 (nand_127_out, in_1, nand_108_out);
  nand nand_128 (nand_128_out, in_1, in_3);
  nand nand_129 (nand_129_out, nand_109_out, nand_109_out);
  nand nand_130 (nand_130_out, nand_110_out, nand_110_out);
  nand nand_131 (nand_131_out, nand_111_out, nand_112_out);
  nand nand_132 (nand_132_out, nand_113_out, nand_114_out);
  nand nand_133 (nand_133_out, nand_115_out, nand_116_out);
  nand nand_134 (nand_134_out, nand_117_out, nand_118_out);
  nand nand_135 (c, nand_119_out, nand_120_out);
  nand nand_136 (nand_136_out, nand_121_out, nand_122_out);
  nand nand_137 (nand_137_out, nand_123_out, nand_124_out);
  nand nand_138 (nand_138_out, nand_125_out, nand_126_out);
  nand nand_139 (nand_139_out, nand_127_out, nand_128_out);
  nand nand_140 (g, nand_129_out, nand_130_out);
  nand nand_141 (nand_141_out, nand_131_out, nand_131_out);
  nand nand_142 (nand_142_out, nand_132_out, nand_132_out);
  nand nand_143 (nand_143_out, nand_133_out, nand_133_out);
  nand nand_144 (nand_144_out, nand_134_out, nand_134_out);
  nand nand_145 (nand_145_out, nand_136_out, nand_136_out);
  nand nand_146 (nand_146_out, nand_137_out, nand_137_out);
  nand nand_147 (nand_147_out, nand_138_out, nand_138_out);
  nand nand_148 (nand_148_out, nand_139_out, nand_139_out);
  nand nand_149 (out_5, nand_141_out, nand_142_out);
  nand nand_150 (b, nand_143_out, nand_144_out);
  nand nand_151 (d, nand_145_out, nand_146_out);
  nand nand_152 (f, nand_147_out, nand_148_out);
  _7_Segment_Display u_7_segment_display_1 ();  // open: g, f, a, b, e, d, c, dp
endmodule

module METRO1 (
  output out_1
);

  wire ACEVEDO_out, BELLO_out, CARIBE_out, clock_1_out, deco7seg_1_b, deco7seg_1_c, deco7seg_1_d,
       deco7seg_1_e, deco7seg_1_f, deco7seg_1_g, deco7seg_1_out_5, FF0_q, FF1_q, FF2_q, HOSPITAL_out,
       MADERA_out, NIQUIA_out, TRICENTENARIO_out, UNIVERSIDAD_out;
  wire [2:0] priority_encoder_1_out;

  Button NIQUIA (.out(NIQUIA_out));
  Button BELLO (.out(BELLO_out));
  Button MADERA (.out(MADERA_out));
  Button ACEVEDO (.out(ACEVEDO_out));
  Button TRICENTENARIO (.out(TRICENTENARIO_out));
  Button CARIBE (.out(CARIBE_out));
  Button UNIVERSIDAD (.out(UNIVERSIDAD_out));
  Button HOSPITAL (.out(HOSPITAL_out));
  Priority_Encoder priority_encoder_1 (
    .in0(NIQUIA_out), .in1(BELLO_out), .in2(MADERA_out), .in3(ACEVEDO_out), .in4(TRICENTENARIO_out),
    .in5(CARIBE_out), .in6(UNIVERSIDAD_out), .in7(HOSPITAL_out), .out(priority_encoder_1_out));  // open: en_in, gs, en_out
  Clock clock_1 (.out(clock_1_out));
  D_Flip_Flop FF0 (.D(priority_encoder_1_out[0]), .clk(clock_1_out), .Q(FF0_q));  // open: Qn, preset, reset
  D_Flip_Flop FF1 (.D(priority_encoder_1_out[1]), .clk(clock_1_out), .Q(FF1_q));  // open: Qn, preset, reset
  D_Flip_Flop FF2 (.D(priority_encoder_1_out[2]), .clk(clock_1_out), .Q(FF2_q));  // open: Qn, preset, reset
  MUX8X1 mux8x1_1 (
    .E0(NIQUIA_out), .E1(BELLO_out), .E2(MADERA_out), .E3(ACEVEDO_out), .E4(TRICENTENARIO_out),
    .E5(CARIBE_out), .E6(UNIVERSIDAD_out), .E7(HOSPITAL_out), .C0(FF0_q), .C1(FF1_q), .C2(FF2_q), .S(out_1));
  DECO7SEG deco7seg_1 (
    .in_2(FF2_q), .in_3(FF1_q), .A(FF0_q), .out_5(deco7seg_1_out_5), .b(deco7seg_1_b), .c(deco7seg_1_c),
    .d(deco7seg_1_d), .e(deco7seg_1_e), .f(deco7seg_1_f), .g(deco7seg_1_g));  // open: in_1
  _7_Segment_Display u_7_segment_display_1 (
    .g(deco7seg_1_g), .f(deco7seg_1_f), .a(deco7seg_1_out_5), .b(deco7seg_1_b), .e(deco7seg_1_e),
    .d(deco7seg_1_d), .c(deco7seg_1_c));  // open: dp
endmodule
