// Logisim project TURNOS.circ as structural Verilog: 3 circuits, main circuit main
module main (
  input  [7:0] TURNO,
  input  CLK,
  output [7:0] TURNO_1,
  output [7:0] TURNO_2,
  output [7:0] TURNO_3,
  output [7:0] TURNO_4
);

  Register R1 (.D(TURNO_2), .en(1'b1), .clk(CLK), .Q(TURNO_1));  // open: clr
  Register R2 (.D(TURNO_3), .en(1'b1), .clk(CLK), .Q(TURNO_2));  // open: clr
  Register R3 (.D(TURNO_4), .en(1'b1), .clk(CLK), .Q(TURNO_3));  // open: clr
  Register R4 (.D(TURNO), .en(1'b1), .clk(CLK), .Q(TURNO_4));  // open: clr
endmodule

module TURNOS_1 (
  input  [7:0] TURNO,
  input  CLK,
  output [7:0] TURNO_1,
  output [7:0] TURNO_2,
  output [7:0] TURNO_3,
  output [7:0] TURNO_4
);

  Register R1 (.D(TURNO_2), .en(1'b1), .clk(CLK), .Q(TURNO_1));  // open: clr
  Register R2 (.D(TURNO_3), .en(1'b1), .clk(CLK), .Q(TURNO_2));  // open: clr
  Register R3 (.D(TURNO_4), .en(1'b1), .clk(CLK), .Q(TURNO_3));  // open: clr
  Register R4 (.D(TURNO), .en(1'b1), .clk(CLK), .Q(TURNO_4));  // open: clr
endmodule

module TURNOS_2 (
  input  [7:0] TURNO,
  input  CLK,
  input  PRIORIDAD,
  output [7:0] TURNO_1,
  output [7:0] TURNO_2,
  output [7:0] TURNO_3,
  output [7:0] TURNO_4
);

  wire not_1_out;
  wire [7:0] multiplexer_1_out;

  Register R1 (.D(multiplexer_1_out), .en(1'b1), .clk(CLK), .Q(TURNO_1));  // open: clr
  Multiplexer #(.width(8)) multiplexer_1 (.in0(TURNO_2), .in1(TURNO), .out(multiplexer_1_out), .sel(PRIORIDAD));
  Register R2 (.D(TURNO_3), .en(not_1_out), .clk(CLK), .Q(TURNO_2));  // open: clr
  Register R3 (.D(TURNO_4), .en(not_1_out), .clk(CLK), .Q(TURNO_3));  // open: clr
  Register R4 (.D(TURNO), .en(not_1_out), .clk(CLK), .Q(TURNO_4));  // open: clr
  not not_1 (not_1_out, PRIORIDAD);
endmodule
