// Logisim project Control_carro_JAGP.circ as structural Verilog: 1 circuit, main circuit main
module main (
  input  in_1,
  input  in_2,
  input  in_3,
  input  in_4,
  input  in_5
);

  wire dipswitch_1_sw1, or_1_out;

  DipSwitch #(.number(2)) dipswitch_1 (.sw1(dipswitch_1_sw1));  // open: sw2
  or or_1 (or_1_out, in_1, in_3, in_4, in_5);
  and and_1 (in_2, or_1_out, dipswitch_1_sw1);
  LED led_1 (.in(in_2));
endmodule
