// Logisim project alu_JAGP.circ as structural Verilog
module Sum_2bits (
  input  A,
  input  B,
  input  Carry,
  output Suma,
  output Carry_s
);

  wire and_1_out, and_2_out, xor_1_out;

  xor xor_1 (xor_1_out, A, B);
  and and_1 (and_1_out, A, B);
  xor xor_2 (Suma, xor_1_out, Carry);
  and and_2 (and_2_out, xor_1_out, Carry);
  or or_1 (Carry_s, and_2_out, and_1_out);
endmodule

module Sum_4bits (
  input  A4,
  input  A3,
  input  A2,
  input  A1,
  input  B4,
  input  B3,
  input  B2,
  input  B1,
  input  Carry,
  output out_10,
  output D4,
  output D3,
  output D2,
  output D1
);

  wire sum_2bits_2_carry_s, sum_2bits_3_carry_s, sum_2bits_4_carry_s;

  Sum_2bits sum_2bits_1 (.A(B4), .B(A4), .Carry(sum_2bits_2_carry_s), .Suma(D4), .Carry_s(out_10));
  Sum_2bits sum_2bits_2 (.A(B3), .B(A3), .Carry(sum_2bits_3_carry_s), .Suma(D3), .Carry_s(sum_2bits_2_carry_s));
  Sum_2bits sum_2bits_3 (.A(B2), .B(A2), .Carry(sum_2bits_4_carry_s), .Suma(D2), .Carry_s(sum_2bits_3_carry_s));
  Sum_2bits sum_2bits_4 (.A(B1), .B(A1), .Carry(Carry), .Suma(D1), .Carry_s(sum_2bits_4_carry_s));
endmodule

module Sumador_Restador_4bits (
  input  A4,
  input  A3,
  input  A2,
  input  A1,
  input  B4,
  input  B3,
  input  B2,
  input  B1,
  input  S_R,
  output Carry_Out,
  output D4,
  output D3,
  output D2,
  output D1
);

  wire sum_2bits_2_carry_s, sum_2bits_3_carry_s, sum_2bits_4_carry_s, xor_1_out, xor_2_out, xor_3_out,
       xor_4_out;

  Sum_2bits sum_2bits_1 (.A(xor_1_out), .B(A4), .Carry(sum_2bits_2_carry_s), .Suma(D4), .Carry_s(Carry_Out));
  Sum_2bits sum_2bits_2 (.A(xor_2_out), .B(A3), .Carry(sum_2bits_3_carry_s), .Suma(D3), .Carry_s(sum_2bits_2_carry_s));
  Sum_2bits sum_2bits_3 (.A(xor_3_out), .B(A2), .Carry(sum_2bits_4_carry_s), .Suma(D2), .Carry_s(sum_2bits_3_carry_s));
  xor xor_1 (xor_1_out, B4, S_R);
  xor xor_2 (xor_2_out, B3, S_R);
  Sum_2bits sum_2bits_4 (.A(xor_4_out), .B(A1), .Carry(S_R), .Suma(D1), .Carry_s(sum_2bits_4_carry_s));
  xor xor_3 (xor_3_out, B2, S_R);
  xor xor_4 (xor_4_out, B1, S_R);
endmodule

module MULTIPLEXADOR (
  input  Control,
  input  A,
  input  B,
  output out_4
);

  wire and_1_out, and_2_out, not_1_out;

  not not_1 (not_1_out, Control);
  and and_1 (and_1_out, not_1_out, A);
  and and_2 (and_2_out, Control, B);
  or or_1 (out_4, and_1_out, and_2_out);
endmodule
