// Logisim project Taller_3_JAGP_CIRCUITOS.circ as structural Verilog
module RON_JAGP (
  input  A,
  input  B,
  output S
);

  wire not_1_out;

  not not_1 (not_1_out, A);
  and and_1 (S, not_1_out, B);
endmodule

module GINEBRA_JAGP (
  input  A,
  input  B,
  output S
);

  wire not_1_out;

  not not_1 (not_1_out, B);
  or or_1 (S, A, not_1_out);
endmodule

module AGUA_JAGP (
  input  in_1,
  input  in_2,
  output out_3
);

  wire and_1_out, and_2_out, not_1_out, not_2_out;

  not not_1 (not_1_out, in_1);
  not not_2 (not_2_out, in_2);
  and and_1 (and_1_out, in_1, not_2_out);
  and and_2 (and_2_out, in_2, not_1_out);
  or or_1 (out_3, and_1_out, and_2_out);
endmodule

module PACHARAN_JAGP (
  input  A,
  input  B,
  input  C,
  output S
);

  wire and_1_out, and_2_out, and_3_out, and_4_out, not_1_out, not_2_out, not_3_out;

  not not_1 (not_1_out, A);
  not not_2 (not_2_out, B);
  not not_3 (not_3_out, C);
  and and_1 (and_1_out, not_1_out, B, C);
  and and_2 (and_2_out, not_2_out, C);
  and and_3 (and_3_out, not_1_out, B, not_3_out);
  and and_4 (and_4_out, A, not_3_out);
  or or_1 (S, and_1_out, and_2_out, and_3_out, and_4_out);
endmodule

module BRANDY_JAGP (
  input  A,
  input  B,
  input  C,
  output S
);

  wire and_1_out, not_1_out, not_2_out;

  not not_1 (not_1_out, A);
  and and_1 (and_1_out, A, C);
  not not_2 (not_2_out, and_1_out);
  or or_1 (S, not_1_out, B, not_2_out);
endmodule

module VINO_JAGP (
  input  A,
  input  B,
  input  C,
  output S
);

  wire and_1_out, nor_1_out, not_1_out, not_2_out;

  not not_1 (not_1_out, A);
  not not_2 (not_2_out, B);
  // OR_Gate or_1 has open pins: in0=not_1_out, in1=not_2_out, out=open
  nor nor_1 (nor_1_out, not_1_out, not_2_out);
  and and_1 (and_1_out, B, C);
  xor xor_1 (S, nor_1_out, and_1_out);
endmodule

module TAGORE_JAGP (
  input  C,
  input  B,
  output out_3
);

  wire not_1_out;

  not not_1 (not_1_out, B);
  or or_1 (out_3, C, not_1_out);
endmodule

module CORTAZA_JAGP (
  input  A,
  input  B,
  input  C,
  output S
);

  wire not_1_out, not_2_out;

  not not_1 (not_1_out, B);
  not not_2 (not_2_out, C);
  and and_1 (S, A, not_1_out, not_2_out);
endmodule

module NERUDA_JAGP (
  input  A,
  input  B,
  input  C,
  output out_4
);

  wire and_1_out, and_2_out, not_1_out, not_2_out;

  not not_1 (not_1_out, A);
  not not_2 (not_2_out, B);
  and and_1 (and_1_out, not_1_out, B);
  and and_2 (and_2_out, not_2_out, C);
  or or_1 (out_4, and_1_out, and_2_out);
endmodule
